# Fritzing sketch ArduinoSensorCO2 (saved by Fritzing 0.9.3b)

parts:
  Part1 = Arduino Uno (Rev3)
  R2 = Resistor [tolerance=±5% resistance=220 package=THT]
  R4 = Resistor [tolerance=±5% resistance=220 package=THT]
  LED1 = LED - 5mm [color="Red (633nm)" package="5 mm [THT]"]
  LED2 = LED - 5mm [color="Green (565nm)" package="5 mm [THT]"]
  Part2 = Adafruit CCS811 [part_number="Adafruit #3566"]
  LCM1602_IIC1 = LCM1602 IIC [part_number="LCM1602 IIC" chip_label="LCM1602 IIC" package="DIP (Dual Inline) [THT]"]

nets:
  N1: Part1.A4/SDA, Part2.SDA, LCM1602_IIC1.SDA
  N2: Part1.A5/SCL, Part2.SCL, LCM1602_IIC1.SCL
  GND: Part1.GND, LED1.cathode, LED2.cathode, Part2.GND, Part2.!WAKE, LCM1602_IIC1.GND
  N3: Part1.D2, R4.Pin_0
  N4: Part1.D3_PWM, R2.Pin_0
  3V3: Part1.3V3, Part2.3.3V
  5V: Part1.5V, LCM1602_IIC1.VCC
  N5: R2.Pin_1, LED1.anode
  N6: R4.Pin_1, LED2.anode

custom parts:
  Adafruit CCS811: Breathe easy - we finally have an I2C VOC/eCO2 sensor in the Adafruit shop! Add air quality monitoring to your project and with an Adafruit CCS811 Air Quality Sensor Breakout. This sensor from AMS is a gas sensor that can detect a wide range of Volatile Organic Compounds (VOCs) and is intended for indoor air quality monitoring. When connected to your microcontroller (running our library code)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
  LCM1602 IIC: I2C-Module to use a 1602 or 2004 LCD on with the wire.h libory Serial LCD Modul
